# Fritzing sketch weathermon_2 (saved by Fritzing 0.7.9b)
stripboards: 2

parts:
  part = BMP085 Breakout  # not connected
  BMP1 = BMP085 Breakout
  DHT1 = DHT22 Humidity and Temperature Sensor

nets:
  VIN: BMP1.VIN, DHT1.VDD
  GND: BMP1.GND, DHT1.GND

custom parts:
  BMP085 Breakout: A breakout for the BMP085 barometric pressure and temperature sensor
